// Logisim project decodificadores.circ as structural Verilog: 1 circuit, main circuit main
module main (
  input  Q7,
  input  Q6,
  input  Q5,
  input  Q4,
  input  Q3,
  input  Q2,
  input  Q1,
  input  Q0,
  input  in_9
);

  wire and_1_out, and_2_out, and_3_out, and_4_out, and_5_out, and_6_out, and_7_out, and_8_out, and_9_out,
       and_10_out, and_11_out, and_12_out, and_13_out, and_14_out, and_15_out, and_16_out, n7447_1_pin9,
       n7447_1_pin10, n7447_1_pin11, n7447_1_pin13, n7447_1_pin15, not_1_out, not_2_out, not_3_out,
       not_4_out, not_5_out, not_6_out, not_7_out, or_1_out, xor_1_out, xor_2_out;

  not not_1 (not_1_out, Q6);
  not not_2 (not_2_out, Q3);
  not not_3 (not_3_out, Q2);
  not not_4 (not_4_out, Q4);
  not not_5 (not_5_out, Q2);
  not not_6 (not_6_out, Q1);
  not not_7 (not_7_out, Q0);
  and and_1 (and_1_out, Q7, not_1_out);
  and and_2 (and_2_out, Q5, Q4);
  and and_3 (and_3_out, not_2_out, not_3_out);
  and and_4 (and_4_out, Q1, Q0);
  and and_5 (and_5_out, Q7, Q6);
  and and_6 (and_6_out, Q5, not_4_out);
  and and_7 (and_7_out, Q3, not_5_out);
  and and_8 (and_8_out, not_6_out, not_7_out);
  and and_9 (and_9_out, and_1_out, and_2_out);
  and and_10 (and_10_out, and_3_out, and_4_out);
  and and_11 (and_11_out, and_5_out, and_6_out);
  and and_12 (and_12_out, and_7_out, and_8_out);
  and and_13 (and_13_out, and_9_out, and_10_out);
  and and_14 (and_14_out, and_11_out, and_12_out);
  LED led_1 (.in(and_13_out));
  LED led_2 (.in(and_14_out));
  or or_1 (or_1_out, and_13_out, and_14_out);
  and and_15 (and_15_out, and_13_out, or_1_out);
  and and_16 (and_16_out, or_1_out, and_14_out);
  xor xor_1 (xor_1_out, and_16_out, n7447_1_pin15);
  _7447 #(.ShowInternalStructure("true")) u_7447_1 (
    .pin1(and_16_out), .pin2(in_9), .pin5(and_15_out), .pin6(and_15_out), .pin7(in_9), .pin15(n7447_1_pin15),
    .pin13(n7447_1_pin13), .pin11(n7447_1_pin11), .pin10(n7447_1_pin10), .pin9(n7447_1_pin9));  // open: pin3, pin4, pin14, pin12
  _7_Segment_Display #(.active("false"), .decimalPoint("false")) u_7_segment_display_1 (
    .g(n7447_1_pin15), .f(xor_1_out), .a(n7447_1_pin13), .b(n7447_1_pin15), .e(n7447_1_pin9), .d(xor_2_out),
    .c(n7447_1_pin11));
  xor xor_2 (xor_2_out, n7447_1_pin10, and_15_out);

  // Notes on the sheet:
  //   Abierto
  //   Cerrado
endmodule
